// Logisim project xor.circ as structural Verilog: 6 circuits, main circuit XOR_1bit
module XOR_1bit (
  input  x,
  input  y,
  output c
);

  wire and_1_out, and_2_out, not_1_out, not_2_out;

  not not_1 (not_1_out, y);
  not not_2 (not_2_out, x);
  and and_1 (and_1_out, x, not_1_out);
  and and_2 (and_2_out, not_2_out, y);
  or or_1 (c, and_1_out, and_2_out);
endmodule

module adder1 (
  input  a,
  input  b,
  input  cin,
  output c,
  output cout
);

  wire and_1_out, and_2_out, or_1_out, xor_1bit_1_c;

  XOR_1bit xor_1bit_1 (.x(a), .y(b), .c(xor_1bit_1_c));
  and and_1 (and_1_out, a, b);
  or or_1 (or_1_out, a, b);
  XOR_1bit xor_1bit_2 (.x(xor_1bit_1_c), .y(cin), .c(c));
  and and_2 (and_2_out, or_1_out, cin);
  or or_2 (cout, and_1_out, and_2_out);
endmodule

module adder4 (
  input  Cin,
  input  [3:0] A,
  input  [3:0] B,
  output [3:0] C,
  output Co3,
  output Cout
);

  wire adder1_1_cout, adder1_2_cout;

  // Probe on A
  // Probe on B
  adder1 adder1_1 (.a(A[0]), .b(B[0]), .cin(Cin), .c(C[0]), .cout(adder1_1_cout));
  adder1 adder1_2 (.a(A[1]), .b(B[1]), .cin(adder1_1_cout), .c(C[1]), .cout(adder1_2_cout));
  adder1 adder1_3 (.a(A[2]), .b(B[2]), .cin(adder1_2_cout), .c(C[2]), .cout(Co3));
  adder1 adder1_4 (.a(A[3]), .b(B[3]), .cin(Co3), .c(C[3]), .cout(Cout));
  // Probe on C
endmodule

module shiftLeft32 (
  input  [4:0] Sa,
  input  Cin,
  input  [31:0] B,
  output [31:0] C
);

  wire [1:0] bit_extender_4_out;
  wire [3:0] bit_extender_3_out;
  wire [7:0] bit_extender_2_out;
  wire [15:0] bit_extender_1_out;
  wire [31:0] multiplexer_1_out, multiplexer_2_out, multiplexer_3_out;
  wire [31:1] multiplexer_4_out_2;
  wire [31:31] multiplexer_4_out;

  // Probe on B
  Bit_Extender #(.in_width(1), .\type ("input")) bit_extender_1 (.in(Cin), .out(bit_extender_1_out));  // open: extend
  // Probe on Sa
  assign bit_extender_2_out = {{7{Cin}}, Cin};  // Bit_Extender bit_extender_2
  Multiplexer #(.width(32), .enable("false")) multiplexer_1 (
    .in0(B), .in1({B[15:0], bit_extender_1_out}), .out(multiplexer_1_out), .sel(Sa[4]));
  assign bit_extender_3_out = {{3{Cin}}, Cin};  // Bit_Extender bit_extender_3
  Multiplexer #(.width(32), .enable("false")) multiplexer_2 (
    .in0(multiplexer_1_out), .in1({multiplexer_1_out[23:0], bit_extender_2_out}), .out(multiplexer_2_out),
    .sel(Sa[3]));
  assign bit_extender_4_out = {{1{Cin}}, Cin};  // Bit_Extender bit_extender_4
  Multiplexer #(.width(32), .enable("false")) multiplexer_3 (
    .in0(multiplexer_2_out), .in1({multiplexer_2_out[27:0], bit_extender_3_out}), .out(multiplexer_3_out),
    .sel(Sa[2]));
  Multiplexer #(.width(32), .enable("false")) multiplexer_4 (
    .in0(multiplexer_3_out), .in1({multiplexer_3_out[29:0], bit_extender_4_out}),
    .out({multiplexer_4_out[31], multiplexer_4_out_2}), .sel(Sa[1]));
  Multiplexer #(.width(32), .enable("false")) multiplexer_5 (
    .in0({multiplexer_4_out[31], multiplexer_4_out_2}), .in1({multiplexer_4_out_2, Cin}), .out(C), .sel(Sa[0]));
  // Probe on C
endmodule

module adder16 (
  input  Cin,
  input  [15:0] A,
  input  [15:0] B,
  output [15:0] C,
  output C15,
  output Cout
);

  wire adder4_1_cout, adder4_2_cout, adder4_3_cout;

  // Probe on A
  // Probe on B
  adder4 adder4_1 (.Cin(Cin), .A(A[3:0]), .B(B[3:0]), .C(C[3:0]), .Cout(adder4_1_cout));  // open: Co3
  adder4 adder4_2 (.Cin(adder4_1_cout), .A(A[7:4]), .B(B[7:4]), .C(C[7:4]), .Cout(adder4_2_cout));  // open: Co3
  adder4 adder4_3 (.Cin(adder4_2_cout), .A(A[11:8]), .B(B[11:8]), .C(C[11:8]), .Cout(adder4_3_cout));  // open: Co3
  adder4 adder4_4 (.Cin(adder4_3_cout), .A(A[15:12]), .B(B[15:12]), .C(C[15:12]), .Co3(C15), .Cout(Cout));
  // Probe on C
endmodule

module adder32 (
  input  [31:0] A,
  input  Cin,
  input  [31:0] B,
  output [31:0] C,
  output V
);

  wire adder16_1_cout, adder16_2_c15, adder16_2_cout;

  // Probe on A
  // Probe on B
  adder16 adder16_1 (.Cin(Cin), .A(A[15:0]), .B(B[15:0]), .C(C[15:0]), .Cout(adder16_1_cout));  // open: C15
  adder16 adder16_2 (
    .Cin(adder16_1_cout), .A(A[31:16]), .B(B[31:16]), .C(C[31:16]), .C15(adder16_2_c15), .Cout(adder16_2_cout));
  // Probe on C
  XOR_1bit xor_1bit_1 (.x(adder16_2_c15), .y(adder16_2_cout), .c(V));
endmodule
