// Logisim project project1_alu.circ as structural Verilog
module ALU32 (
  input  [3:0] op,
  input  [31:0] A,
  input  [31:0] B,
  input  [4:0] Sa,
  output [31:0] C,
  output V
);

  wire adder32_1_v, Ag0, controlunit_1_addercin, controlunit_1_compareinst, controlunit_1_inverta,
       controlunit_1_invertaob, controlunit_1_invertb, controlunit_1_isarith, controlunit_1_shiftarith,
       controlunit_1_shiftr, multiplexer_6_out, multiplexer_7_out, nor_1_out, not_4_out, not_5_out, or_1_out;
  wire [0:0] multiplexer_8_out;
  wire [1:0] controlunit_1_outputsel;
  wire [31:0] adder32_1_c, multiplexer_1_out, multiplexer_2_out, multiplexer_3_out, multiplexer_4_out,
       multiplexer_9_out, multiplexer_10_out, not_1_out, not_2_out, not_3_out, or_2_out, shiftleft32_1_c,
       xor_1_out;

  // Probe on A
  assign not_1_out = ~A;  // NOT_Gate not_1, 32 bits wide
  assign not_2_out = ~B;  // NOT_Gate not_2, 32 bits wide
  or or_1 (or_1_out, A[0], A[1], A[2], A[3], A[4], A[5], A[6], A[7], A[8], A[9], A[10], A[11], A[12], A[13], A[14], A[15], A[16], A[17], A[18], A[19], A[20], A[21], A[22], A[23], A[24], A[25], A[26], A[27], A[28], A[29], A[30]);
  Multiplexer #(.width(32), .enable("false")) multiplexer_1 (
    .in0(A), .in1(not_1_out), .out(multiplexer_1_out), .sel(controlunit_1_inverta));
  Multiplexer #(.width(32), .enable("false")) multiplexer_2 (
    .in0(B), .in1(not_2_out), .out(multiplexer_2_out), .sel(controlunit_1_invertb));
  // Probe on B
  // Probe on B
  and AOpsitive (Ag0, or_1_out, ~A[31]);  // AND_Gate
  assign or_2_out = multiplexer_1_out | multiplexer_2_out;  // OR_Gate or_2, 32 bits wide
  assign xor_1_out = multiplexer_1_out ^ multiplexer_2_out;  // XOR_Gate xor_1, 32 bits wide
  assign not_3_out = ~or_2_out;  // NOT_Gate not_3, 32 bits wide
  adder32 adder32_1 (
    .A(multiplexer_1_out), .Cin(controlunit_1_addercin), .B(multiplexer_2_out), .C(adder32_1_c),
    .V(adder32_1_v));
  Multiplexer #(.width(32), .enable("false")) multiplexer_3 (
    .in0(or_2_out), .in1(not_3_out), .out(multiplexer_3_out), .sel(controlunit_1_invertaob));
  Multiplexer #(.width(32), .enable("false")) multiplexer_4 (
    .in0(multiplexer_2_out),
    .in1({multiplexer_2_out[0], multiplexer_2_out[1], multiplexer_2_out[2], multiplexer_2_out[3], multiplexer_2_out[4], multiplexer_2_out[5], multiplexer_2_out[6], multiplexer_2_out[7], multiplexer_2_out[8], multiplexer_2_out[9], multiplexer_2_out[10], multiplexer_2_out[11], multiplexer_2_out[12], multiplexer_2_out[13], multiplexer_2_out[14], multiplexer_2_out[15], multiplexer_2_out[16], multiplexer_2_out[17], multiplexer_2_out[18], multiplexer_2_out[19], multiplexer_2_out[20], multiplexer_2_out[21], multiplexer_2_out[22], multiplexer_2_out[23], multiplexer_2_out[24], multiplexer_2_out[25], multiplexer_2_out[26], multiplexer_2_out[27], multiplexer_2_out[28], multiplexer_2_out[29], multiplexer_2_out[30], multiplexer_2_out[31]}),
    .out(multiplexer_4_out), .sel(controlunit_1_shiftr));
  Multiplexer #(.enable("false")) multiplexer_5 (.in0(1'b0), .in1(adder32_1_v), .out(V), .sel(controlunit_1_isarith));
  controlUnit controlunit_1 (
    .opCode(op), .invertA(controlunit_1_inverta), .invertB(controlunit_1_invertb),
    .invertAoB(controlunit_1_invertaob), .compareInst(controlunit_1_compareinst),
    .isArith(controlunit_1_isarith), .shiftR(controlunit_1_shiftr), .adderCin(controlunit_1_addercin),
    .outputSel(controlunit_1_outputsel), .shiftArith(controlunit_1_shiftarith));
  Multiplexer #(.enable("false")) multiplexer_6 (
    .in0(1'b0), .in1(B[31]), .out(multiplexer_6_out), .sel(controlunit_1_shiftarith));
  nor nor_1 (nor_1_out, adder32_1_c[0], adder32_1_c[1], adder32_1_c[2], adder32_1_c[3], adder32_1_c[4], adder32_1_c[5], adder32_1_c[6], adder32_1_c[7], adder32_1_c[8], adder32_1_c[9], adder32_1_c[10], adder32_1_c[11], adder32_1_c[12], adder32_1_c[13], adder32_1_c[14], adder32_1_c[15], adder32_1_c[17], adder32_1_c[18], adder32_1_c[19], adder32_1_c[20], adder32_1_c[21], adder32_1_c[22], adder32_1_c[23], adder32_1_c[24], adder32_1_c[25], adder32_1_c[26], adder32_1_c[27], adder32_1_c[28], adder32_1_c[29], adder32_1_c[30], adder32_1_c[31], adder32_1_c[16]);
  Multiplexer #(.enable("false")) multiplexer_7 (.in0(nor_1_out), .in1(Ag0), .out(multiplexer_7_out), .sel(op[2]));
  shiftLeft32 shiftleft32_1 (
    .Sa(Sa), .Cin(multiplexer_6_out), .B(multiplexer_4_out),
    .C({shiftleft32_1_c[0], shiftleft32_1_c[1], shiftleft32_1_c[2], shiftleft32_1_c[3], shiftleft32_1_c[4], shiftleft32_1_c[5], shiftleft32_1_c[6], shiftleft32_1_c[7], shiftleft32_1_c[8], shiftleft32_1_c[9], shiftleft32_1_c[10], shiftleft32_1_c[11], shiftleft32_1_c[12], shiftleft32_1_c[13], shiftleft32_1_c[14], shiftleft32_1_c[15], shiftleft32_1_c[16], shiftleft32_1_c[17], shiftleft32_1_c[18], shiftleft32_1_c[19], shiftleft32_1_c[20], shiftleft32_1_c[21], shiftleft32_1_c[22], shiftleft32_1_c[23], shiftleft32_1_c[24], shiftleft32_1_c[25], shiftleft32_1_c[26], shiftleft32_1_c[27], shiftleft32_1_c[28], shiftleft32_1_c[29], shiftleft32_1_c[30], shiftleft32_1_c[31]}));
  not not_4 (not_4_out, op[1]);
  Multiplexer #(.enable("false")) multiplexer_8 (
    .in0(multiplexer_7_out), .in1(not_5_out), .out(multiplexer_8_out[0]), .sel(not_4_out));
  not not_5 (not_5_out, multiplexer_7_out);
  Multiplexer #(.width(32), .enable("false")) multiplexer_9 (
    .in0(adder32_1_c), .in1({{31{1'b0}}, multiplexer_8_out[0]}), .out(multiplexer_9_out),
    .sel(controlunit_1_compareinst));
  Multiplexer #(.width(32), .enable("false")) multiplexer_10 (
    .in0({shiftleft32_1_c[0], shiftleft32_1_c[1], shiftleft32_1_c[2], shiftleft32_1_c[3], shiftleft32_1_c[4], shiftleft32_1_c[5], shiftleft32_1_c[6], shiftleft32_1_c[7], shiftleft32_1_c[8], shiftleft32_1_c[9], shiftleft32_1_c[10], shiftleft32_1_c[11], shiftleft32_1_c[12], shiftleft32_1_c[13], shiftleft32_1_c[14], shiftleft32_1_c[15], shiftleft32_1_c[16], shiftleft32_1_c[17], shiftleft32_1_c[18], shiftleft32_1_c[19], shiftleft32_1_c[20], shiftleft32_1_c[21], shiftleft32_1_c[22], shiftleft32_1_c[23], shiftleft32_1_c[24], shiftleft32_1_c[25], shiftleft32_1_c[26], shiftleft32_1_c[27], shiftleft32_1_c[28], shiftleft32_1_c[29], shiftleft32_1_c[30], shiftleft32_1_c[31]}),
    .in1(shiftleft32_1_c), .out(multiplexer_10_out), .sel(controlunit_1_shiftr));
  Multiplexer #(.select(2), .width(32), .enable("false")) multiplexer_11 (
    .in0(multiplexer_3_out), .in1(xor_1_out), .in2(multiplexer_9_out), .in3(multiplexer_10_out), .out(C),
    .sel(controlunit_1_outputsel));
  // Probe on C
  // Probe on C

  // Other names for the same wires on the sheet: Bsign = B[31]
endmodule

module XOR_1bit (
  input  x,
  input  y,
  output c
);

  wire and_1_out, and_2_out, not_1_out, not_2_out;

  not not_1 (not_1_out, y);
  not not_2 (not_2_out, x);
  and and_1 (and_1_out, x, not_1_out);
  and and_2 (and_2_out, not_2_out, y);
  or or_1 (c, and_1_out, and_2_out);
endmodule

module adder1 (
  input  a,
  input  b,
  input  cin,
  output c,
  output cout
);

  wire and_1_out, and_2_out, or_1_out, xor_1bit_1_c;

  XOR_1bit xor_1bit_1 (.x(a), .y(b), .c(xor_1bit_1_c));
  and and_1 (and_1_out, a, b);
  or or_1 (or_1_out, a, b);
  XOR_1bit xor_1bit_2 (.x(xor_1bit_1_c), .y(cin), .c(c));
  and and_2 (and_2_out, or_1_out, cin);
  or or_2 (cout, and_1_out, and_2_out);
endmodule

module adder4 (
  input  Cin,
  input  [3:0] A,
  input  [3:0] B,
  output [3:0] C,
  output Co3,
  output Cout
);

  wire adder1_1_cout, adder1_2_cout;

  // Probe on A
  // Probe on B
  adder1 adder1_1 (.a(A[0]), .b(B[0]), .cin(Cin), .c(C[0]), .cout(adder1_1_cout));
  adder1 adder1_2 (.a(A[1]), .b(B[1]), .cin(adder1_1_cout), .c(C[1]), .cout(adder1_2_cout));
  adder1 adder1_3 (.a(A[2]), .b(B[2]), .cin(adder1_2_cout), .c(C[2]), .cout(Co3));
  adder1 adder1_4 (.a(A[3]), .b(B[3]), .cin(Co3), .c(C[3]), .cout(Cout));
  // Probe on C
endmodule

module shiftLeft32 (
  input  [4:0] Sa,
  input  Cin,
  input  [31:0] B,
  output [31:0] C
);

  wire [1:0] bit_extender_4_out;
  wire [3:0] bit_extender_3_out;
  wire [7:0] bit_extender_2_out;
  wire [15:0] bit_extender_1_out;
  wire [31:0] multiplexer_1_out, multiplexer_2_out, multiplexer_3_out;
  wire [31:1] multiplexer_4_out_2;
  wire [31:31] multiplexer_4_out;

  // Probe on B
  assign bit_extender_1_out = {{15{Cin}}, Cin};  // Bit_Extender bit_extender_1
  // Probe on Sa
  assign bit_extender_2_out = {{7{Cin}}, Cin};  // Bit_Extender bit_extender_2
  Multiplexer #(.width(32), .enable("false")) multiplexer_1 (
    .in0(B), .in1({B[15:0], bit_extender_1_out}), .out(multiplexer_1_out), .sel(Sa[4]));
  assign bit_extender_3_out = {{3{Cin}}, Cin};  // Bit_Extender bit_extender_3
  Multiplexer #(.width(32), .enable("false")) multiplexer_2 (
    .in0(multiplexer_1_out), .in1({multiplexer_1_out[23:0], bit_extender_2_out}), .out(multiplexer_2_out),
    .sel(Sa[3]));
  assign bit_extender_4_out = {{1{Cin}}, Cin};  // Bit_Extender bit_extender_4
  Multiplexer #(.width(32), .enable("false")) multiplexer_3 (
    .in0(multiplexer_2_out), .in1({multiplexer_2_out[27:0], bit_extender_3_out}), .out(multiplexer_3_out),
    .sel(Sa[2]));
  Multiplexer #(.width(32), .enable("false")) multiplexer_4 (
    .in0(multiplexer_3_out), .in1({multiplexer_3_out[29:0], bit_extender_4_out}),
    .out({multiplexer_4_out[31], multiplexer_4_out_2}), .sel(Sa[1]));
  Multiplexer #(.width(32), .enable("false")) multiplexer_5 (
    .in0({multiplexer_4_out[31], multiplexer_4_out_2}), .in1({multiplexer_4_out_2, Cin}), .out(C), .sel(Sa[0]));
  // Probe on C
endmodule

module adder16 (
  input  Cin,
  input  [15:0] A,
  input  [15:0] B,
  output [15:0] C,
  output C15,
  output Cout
);

  wire adder4_1_cout, adder4_2_cout, adder4_3_cout;

  // Probe on A
  // Probe on B
  adder4 adder4_1 (.Cin(Cin), .A(A[3:0]), .B(B[3:0]), .C(C[3:0]), .Cout(adder4_1_cout));  // open: Co3
  adder4 adder4_2 (.Cin(adder4_1_cout), .A(A[7:4]), .B(B[7:4]), .C(C[7:4]), .Cout(adder4_2_cout));  // open: Co3
  adder4 adder4_3 (.Cin(adder4_2_cout), .A(A[11:8]), .B(B[11:8]), .C(C[11:8]), .Cout(adder4_3_cout));  // open: Co3
  adder4 adder4_4 (.Cin(adder4_3_cout), .A(A[15:12]), .B(B[15:12]), .C(C[15:12]), .Co3(C15), .Cout(Cout));
  // Probe on C
endmodule

module adder32 (
  input  [31:0] A,
  input  Cin,
  input  [31:0] B,
  output [31:0] C,
  output V
);

  wire adder16_1_cout, adder16_2_c15, adder16_2_cout;

  // Probe on A
  // Probe on B
  adder16 adder16_1 (.Cin(Cin), .A(A[15:0]), .B(B[15:0]), .C(C[15:0]), .Cout(adder16_1_cout));  // open: C15
  adder16 adder16_2 (
    .Cin(adder16_1_cout), .A(A[31:16]), .B(B[31:16]), .C(C[31:16]), .C15(adder16_2_c15), .Cout(adder16_2_cout));
  // Probe on C
  XOR_1bit xor_1bit_1 (.x(adder16_2_c15), .y(adder16_2_cout), .c(V));
endmodule

module controlUnit (
  input  [3:0] opCode,
  output invertA,
  output invertB,
  output invertAoB,
  output compareInst,
  output isArith,
  output shiftR,
  output adderCin,
  output [1:0] outputSel,
  output shiftArith
);

  controlSub controlsub_1 (
    .a(opCode[3]), .b(opCode[2]), .c(opCode[1]), .d(opCode[0]), .invertA(invertA), .invertB(invertB),
    .invertAoB(invertAoB), .compareInst(compareInst), .isArith(isArith), .shiftR(shiftR),
    .adderCin(adderCin), .outputSel1(outputSel[1]), .outpustSel0(outputSel[0]), .shiftArith(shiftArith));
endmodule

module controlSub (
  input  a,
  input  b,
  input  c,
  input  d,
  output invertA,
  output invertB,
  output invertAoB,
  output compareInst,
  output isArith,
  output shiftR,
  output adderCin,
  output outputSel1,
  output outpustSel0,
  output shiftArith
);

  wire and_4_out, and_5_out, and_6_out, and_9_out, and_10_out, not_1_out, not_2_out, not_3_out, not_4_out,
       not_5_out, not_6_out, not_7_out, not_8_out, not_9_out, not_10_out, not_11_out, not_12_out, not_13_out,
       not_14_out, not_15_out, or_1_out, or_4_out, xor_1_out;

  not not_1 (not_1_out, a);
  not not_2 (not_2_out, b);
  not not_3 (not_3_out, c);
  not not_4 (not_4_out, a);
  not not_5 (not_5_out, b);
  or or_1 (or_1_out, c, not_6_out);
  not not_6 (not_6_out, d);
  xor xor_1 (xor_1_out, b, c);
  not not_7 (not_7_out, a);
  not not_8 (not_8_out, a);
  and and_1 (compareInst, not_8_out, not_9_out);
  not not_9 (not_9_out, d);
  and and_2 (isArith, a, not_10_out);
  not not_10 (not_10_out, c);
  and and_3 (shiftR, a, b, c);
  not not_11 (not_11_out, a);
  not not_12 (not_12_out, b);
  and and_4 (and_4_out, not_11_out, not_12_out, not_13_out);
  not not_13 (not_13_out, d);
  and and_5 (and_5_out, a, b, not_14_out);
  not not_14 (not_14_out, c);
  or or_2 (outputSel1, a, not_15_out);
  not not_15 (not_15_out, d);
  and and_6 (and_6_out, b, d);
  and and_7 (shiftArith, b, d);
  and and_8 (invertA, not_1_out, not_2_out, c, d);
  and and_9 (and_9_out, a, b, not_3_out);
  and and_10 (and_10_out, not_4_out, not_5_out, or_1_out);
  and and_11 (invertAoB, xor_1_out, not_7_out, d);
  or or_3 (adderCin, and_4_out, and_5_out);
  and and_12 (outpustSel0, c, or_4_out);
  or or_4 (or_4_out, a, and_6_out);
  or or_5 (invertB, and_9_out, and_10_out);
endmodule

module test (
  input  [7:0] in_1,
  input  [7:0] in_2
);

  wire [7:0] and_1_out;

  assign and_1_out = in_1 & in_2;  // AND_Gate and_1, 8 bits wide
endmodule
