// Logisim project miniRISCV.circ as structural Verilog
module singleClock (
);

  wire registerfile_1_p5;
  wire [31:0] alu_1_p3, immgen_1_immediate, multiplexer_2_out, PC_q, registerfile_1_p1, registerfile_1_p6,
       risc_vprogramrom_1_p2;

  Register #(.width(32)) PC (.Q(PC_q));  // open: D, en, clk, clr
  // RISC_VProgramROM risc_vprogramrom_1: pin names not known; wires that end beside it: PC_q, risc_vprogramrom_1_p2
  // RegisterFile registerfile_1: pin names not known; wires that end beside it: registerfile_1_p1, risc_vprogramrom_1_p2[11:7], risc_vprogramrom_1_p2[19:15], risc_vprogramrom_1_p2[24:20], registerfile_1_p5, registerfile_1_p6
  Multiplexer #(.width(32), .enable("false")) multiplexer_1 (
    .in0(immgen_1_immediate), .in1(alu_1_p3), .out(registerfile_1_p1));  // open: sel
  immGen immgen_1 (.in_1(risc_vprogramrom_1_p2), .immediate(immgen_1_immediate));
  Multiplexer #(.width(32), .enable("false")) multiplexer_2 (
    .in0(registerfile_1_p6), .in1(immgen_1_immediate), .out(multiplexer_2_out));  // open: sel
  // ALU alu_1: pin names not known; wires that end beside it: registerfile_1_p5, multiplexer_2_out, alu_1_p3
endmodule

module immGen (
  input  [31:0] in_1,
  output [31:0] immediate
);

  wire [2:0] opcode;

  immTypeRecog immtyperecog_1 (
    .a(in_1[6]), .b(in_1[5]), .c(in_1[4]), .d(in_1[3]), .e(in_1[2]), .f(in_1[1]), .g(in_1[0]), .x(opcode[2]),
    .y(opcode[1]), .z(opcode[0]));
  Multiplexer #(.select(3), .width(32), .enable("false")) multiplexer_1 (
    .in0({32{1'b0}}), .in1({{20{1'b0}}, in_1[31:20]}), .in2({in_1[31:12], {12{1'b0}}}),
    .in3({in_1[31], in_1[19:12], in_1[20], in_1[30:21], {12{1'b0}}}),
    .in4({{19{1'b0}}, in_1[31], in_1[7], in_1[30:25], in_1[11:8], 1'b0}),
    .in5({{20{1'b0}}, in_1[31:25], in_1[11:7]}), .in6({32{1'b0}}), .in7({32{1'b0}}), .out(immediate),
    .sel(opcode));
endmodule

module immTypeRecog (
  input  a,
  input  b,
  input  c,
  input  d,
  input  e,
  input  f,
  input  g,
  output x,
  output y,
  output z
);

  wire and_2_out, and_3_out, and_4_out, and_5_out, and_6_out, not_1_out, not_2_out, not_3_out, not_4_out,
       not_5_out, not_6_out, not_7_out, not_8_out, not_9_out, not_10_out, not_11_out, not_12_out, not_13_out,
       not_14_out, not_15_out;

  not not_1 (not_1_out, c);
  not not_2 (not_2_out, d);
  not not_3 (not_3_out, e);
  not not_4 (not_4_out, a);
  not not_5 (not_5_out, d);
  not not_6 (not_6_out, c);
  not not_7 (not_7_out, a);
  not not_8 (not_8_out, b);
  not not_9 (not_9_out, d);
  not not_10 (not_10_out, e);
  not not_11 (not_11_out, a);
  not not_12 (not_12_out, c);
  not not_13 (not_13_out, d);
  not not_14 (not_14_out, e);
  not not_15 (not_15_out, c);
  and and_1 (x, b, not_1_out, not_2_out, not_3_out, f, g);
  and and_2 (and_2_out, not_4_out, c, not_5_out, e, f, g);
  and and_3 (and_3_out, a, b, not_6_out, d, e, f, g);
  and and_4 (and_4_out, not_7_out, not_8_out, c, not_9_out, not_10_out, f, g);
  and and_5 (and_5_out, not_11_out, b, not_12_out, not_13_out, not_14_out, f, g);
  and and_6 (and_6_out, a, b, not_15_out, e, f, g);
  or or_1 (y, and_2_out, and_3_out);
  or or_2 (z, and_4_out, and_5_out, and_6_out);
endmodule
